# Fritzing sketch Gains_Box (saved by Fritzing 1.0.1rc)
breadboards: 2

parts:
  A1 = Particle - Photon2  # not connected
  SW1 = ENCODER_RGB_CA [package=encoder_led_3]
  HC-SR04_Sensor_1 = HC-SR04 Ultrasonic Distance Sensor
  Mod1 = Passive Buzzer
  Neopixel1 = Adafruit RBG Smart Neopixel [package="DIP (Dual Inline) [THT]"]
  Neopixel2 = Adafruit RBG Smart Neopixel [package="DIP (Dual Inline) [THT]"]
  Grove1 = Grove OLED 128x96

nets:
  GND: SW1.-B, HC-SR04_Sensor_1.GND, Mod1.-, Neopixel1.G, Neopixel2.G, Grove1.GND
  N1: SW1.+, Mod1.NC, Grove1.VCC
  N2: Neopixel1.O, Neopixel2.In
  N3: Neopixel1.+, Neopixel2.+

custom parts:
  Particle - Photon2: The Photon 2 is a microcontroller and Wi-Fi networking developed by particle. Features: 802.11a/b/g/n Wi-Fi, 2.4 GHz and 5 GHz Integrated PCB antenna Integrated U.FL connector for external antenna Integrated RF switch BLE 5 using same antenna as Wi-Fi Realtek RTL8721DM MCU ARM Cortex M33 CPU, 200 MHz 2048 KB (2 MB) user application maximum size 3072 KB (3 MB) of RAM available to user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
